// Digital circuit flush-mux.dig as structural Verilog
module flush_mux (
  input  [3:0] M_id,
  input  M_ep,
  input  [3:0] J_id,
  input  J_ep,
  input  M_v,
  input  J_v,
  input  [3:0] I_id,
  input  I_ep,
  input  I_v,
  input  [3:0] E_id,
  input  E_v,
  input  E_ep,
  input  [3:0] T_id,
  input  T_ep,
  input  T_v,
  output [3:0] m_id_2,
  output m_ep_2,
  output m_v_2,
  output sel
);

  wire comparator_1_gt, comparator_1_lt, multiplexer_1_out, multiplexer_3_out, multiplexer_5_out,
       multiplexer_7_out, not_1_out, or_1_out, or_2_out, or_4_out, xor_1_out;
  wire [3:0] multiplexer_2_out, multiplexer_4_out, multiplexer_6_out;

  Comparator #(.Bits(4)) comparator_1 (.a(M_id), .b(J_id), .gt(comparator_1_gt), .lt(comparator_1_lt));  // open: eq
  xor xor_1 (xor_1_out, M_ep, J_ep);
  Multiplexer multiplexer_1 (.sel(xor_1_out), .in_0(comparator_1_gt), .in_1(comparator_1_lt), .out(multiplexer_1_out));
  Multiplexer #(.Bits(4)) multiplexer_2 (.sel(sel), .in_0(J_id), .in_1(M_id), .out(multiplexer_2_out));
  Multiplexer multiplexer_3 (.sel(sel), .in_0(J_ep), .in_1(M_ep), .out(multiplexer_3_out));
  or or_1 (or_1_out, J_v, I_v, E_v, T_v);
  or or_2 (or_2_out, I_v, E_v, T_v, not_1_out, multiplexer_1_out);
  not not_1 (not_1_out, M_v);
  Multiplexer #(.Bits(4)) multiplexer_4 (.sel(I_v), .in_0(T_id), .in_1(I_id), .out(multiplexer_4_out));
  Multiplexer multiplexer_5 (.sel(I_v), .in_0(T_ep), .in_1(I_ep), .out(multiplexer_5_out));
  nand nand_1 (sel, or_1_out, or_2_out);
  or or_3 (m_v_2, M_v, J_v, I_v, E_v, T_v);
  or or_4 (or_4_out, I_v, E_v, T_v);
  Multiplexer #(.Bits(4)) multiplexer_6 (.sel(E_v), .in_0(multiplexer_4_out), .in_1(E_id), .out(multiplexer_6_out));
  Multiplexer multiplexer_7 (.sel(E_v), .in_0(multiplexer_5_out), .in_1(E_ep), .out(multiplexer_7_out));
  Multiplexer #(.Bits(4)) multiplexer_8 (
    .sel(or_4_out), .in_0(multiplexer_2_out), .in_1(multiplexer_6_out), .out(m_id_2));
  Multiplexer multiplexer_9 (.sel(or_4_out), .in_0(multiplexer_3_out), .in_1(multiplexer_7_out), .out(m_ep_2));
endmodule
