// Digital circuit res-station.dig as structural Verilog
module res_station (
  input  C,
  input  res,
  input  [3:0] inst,
  input  URA,
  input  URB,
  input  [4:0] RA,
  input  [4:0] RB,
  input  USC,
  input  UFL,
  input  ORC,
  input  [4:0] RC,
  input  OSC,
  input  OFL,
  input  com1,
  input  com2,
  input  [3:0] com1_inst,
  input  [3:0] com2_inst,
  input  [4:0] com1_OR,
  input  [4:0] com2_OR,
  input  [3:0] com1_OSC,
  input  [3:0] com2_OSC,
  input  [3:0] com1_OFL,
  input  [3:0] com2_OFL,
  input  E,
  input  [31:0] D,
  input  clr,
  input  ep_I,
  input  [7:0] FU_free,
  input  [2:0] UFU,
  input  [3:0] clr_id,
  input  clr_ep,
  output V,
  output [3:0] disp,
  output full,
  output [31:0] disp_32,
  output ep_O
);

  wire and_1_out, and_7_out, and_12_out, and_20_out, and_23_out, and_28_out, and_33_out, and_40_out,
       and_43_out, bitselector_1_out, bitselector_2_out, bitselector_3_out, bitselector_4_out,
       bitselector_5_out, bitselector_6_out, bitselector_7_out, bitselector_8_out, comparator_1_eq,
       comparator_2_eq, comparator_3_eq, comparator_4_eq, fill_8_1_v, FL_com1, FL_com2, or_1_out, or_2_out,
       or_3_out, priority_test8_1_out1, priority_test8_1_out2, priority_test8_1_out3, priority_test8_1_out4,
       priority_test8_1_out5, priority_test8_1_out6, priority_test8_1_out7, priority_test8_1_out8,
       priorityencoder_1_any, SC_com1, SC_com2;
  wire [2:0] and_8_out, and_9_out, and_10_out, and_13_out, and_14_out, and_15_out, and_18_out, and_19_out,
       and_21_out, and_24_out, and_25_out, and_26_out, and_29_out, and_30_out, and_31_out, and_34_out,
       and_35_out, and_36_out, and_38_out, and_39_out, and_41_out, and_44_out, and_45_out, and_46_out,
       and_48_out, and_49_out, bitextender_1_out, bitextender_2_out, bitextender_3_out, bitextender_4_out,
       bitextender_5_out, bitextender_6_out, bitextender_9_out, bitextender_10_out, bitextender_11_out,
       bitextender_12_out, bitextender_13_out, bitextender_14_out, bitextender_15_out, bitextender_16_out,
       bitextender_17_out, bitextender_18_out, bitextender_19_out, bitextender_20_out, bitextender_21_out,
       bitextender_22_out, bitextender_23_out, bitextender_24_out, bitextender_25_out, bitextender_26_out,
       bitextender_27_out, bitextender_28_out, comparator_5_eq, comparator_8_eq, comparator_11_eq,
       comparator_14_eq, comparator_17_eq, comparator_20_eq, comparator_23_eq, comparator_26_eq,
       comparator_29_eq, comparator_32_eq, comparator_35_eq, comparator_38_eq, comparator_41_eq,
       comparator_44_eq, comparator_47_eq, comparator_50_eq, comparator_53_eq, comparator_56_eq,
       multiplexer_3_out_2, multiplexer_15_out, multiplexer_16_out, multiplexer_17_out, multiplexer_18_out,
       multiplexer_19_out, multiplexer_20_out, multiplexer_21_out, multiplexer_22_out, or_6_out, or_7_out,
       or_8_out, or_10_out, or_11_out, or_13_out, or_14_out, or_15_out, or_16_out, or_17_out, or_18_out,
       or_19_out, or_20_out, or_21_out, or_22_out, or_23_out, or_24_out, priorityencoder_1_num,
       register_17_q_2, rs_ff_1_q, rs_ff_4_q, rs_ff_7_q, rs_ff_10_q, rs_ff_13_q, rs_ff_16_q, rs_ff_19_q,
       rs_ff_22_q;
  wire [3:0] multiplexer_3_out, multiplexer_4_out, multiplexer_5_out, register_2_q, register_5_q,
       register_8_q, register_11_q, register_14_q, register_20_q, register_23_q;
  wire [4:0] FL, inst_wfile_1_r_a, inst_wfile_1_r_b, multiplexer_6_out, SC;
  wire [4:4] register_2_q_2, register_5_q_2, register_8_q_2, register_11_q_2, register_14_q_2,
       register_20_q_2, register_23_q_2;
  wire [5:0] multiplexer_1_out, multiplexer_2_out;
  wire [7:0] and_6_out, and_16_out, and_47_out, bitextender_7_out, bitextender_8_out, clr_8,
       demultiplexer_1_out_0, fill_8_1_out1, inst_comp_8_a_old, multiplexer_7_out, not_1_out, not_3_out,
       not_4_out, not_5_out, or_5_out, register_22_q;
  wire [7:1] or_4_out;
  wire [7:7] or_4_out_2;
  wire [14:0] register_2_q_3, register_5_q_3, register_8_q_3, register_11_q_3, register_14_q_3,
       register_20_q_3, register_23_q_3;
  wire [19:0] register_17_q;
  wire [31:0] register_3_q, register_6_q, register_9_q, register_12_q, register_15_q, register_18_q,
       register_21_q, register_24_q;

  Multiplexer #(.Bits(6)) multiplexer_1 (
    .sel(OSC), .in_0(6'b100000), .in_1({1'b0, ep_I, inst}), .out(multiplexer_1_out));
  Multiplexer #(.Bits(6)) multiplexer_2 (
    .sel(OFL), .in_0(6'b100000), .in_1({1'b0, ep_I, inst}), .out(multiplexer_2_out));
  and and_1 (and_1_out, E, ORC);
  or or_1 (or_1_out, OSC, SC_com1, SC_com2);
  or or_2 (or_2_out, OFL, FL_com1, FL_com2);
  Comparator #(.Bits(4)) comparator_1 (.a(com2_inst), .b(SC[3:0]), .eq(comparator_1_eq));  // open: gt, lt
  and and_2 (SC_com2, comparator_1_eq, ~SC[4], com2);  // And
  Comparator #(.Bits(4)) comparator_2 (.a(com1_inst), .b(SC[3:0]), .eq(comparator_2_eq));  // open: gt, lt
  and and_3 (SC_com1, comparator_2_eq, ~SC[4], com1);  // And
  fill_8 fill_8_1 (
    .on(1'b0), .in1(not_1_out[0]), .in2(not_1_out[1]), .in3(not_1_out[2]), .in4(not_1_out[3]),
    .in5(not_1_out[4]), .in6(not_1_out[5]), .in7(not_1_out[6]), .in8(not_1_out[7]), .out1(fill_8_1_out1[0]),
    .out2(fill_8_1_out1[1]), .out3(fill_8_1_out1[2]), .out4(fill_8_1_out1[3]), .out5(fill_8_1_out1[4]),
    .out6(fill_8_1_out1[5]), .out7(fill_8_1_out1[6]), .out8(fill_8_1_out1[7]), .v(fill_8_1_v));
  assign not_1_out = ~register_22_q;  // Not not_1, 8 bits wide
  inst_wfile inst_wfile_1 (
    .C(C), .res(res), .E1(and_1_out), .com1(com1), .com2(com2), .I_com1(com1_inst), .I_com2(com2_inst),
    .Inst({ep_I, inst}), .W(RC), .W_com1(com1_OR), .W_com2(com2_OR), .RA(RA), .RB(RB),
    .SC_inst(multiplexer_1_out), .SC_sel(or_1_out), .SC_e(1'b1), .FL_inst(multiplexer_2_out),
    .FL_sel(or_2_out), .FL_e(1'b1), .clr(clr), .clr_ep(clr_ep), .clr_id(clr_id), .R_A(inst_wfile_1_r_a),
    .R_B(inst_wfile_1_r_b), .SC_O(SC), .FL_O(FL));
  Comparator #(.Bits(4)) comparator_3 (.a(com2_inst), .b(FL[3:0]), .eq(comparator_3_eq));  // open: gt, lt
  and and_4 (FL_com2, comparator_3_eq, ~FL[4], com2);  // And
  Comparator #(.Bits(4)) comparator_4 (.a(com1_inst), .b(FL[3:0]), .eq(comparator_4_eq));  // open: gt, lt
  and and_5 (FL_com1, comparator_4_eq, ~FL[4], com1);  // And
  Demultiplexer #(.Selector_Bits(3)) demultiplexer_1 (
    .sel(priorityencoder_1_num), .in(priorityencoder_1_any), .out_0(demultiplexer_1_out_0[0]),
    .out_1(demultiplexer_1_out_0[1]), .out_2(demultiplexer_1_out_0[2]), .out_3(demultiplexer_1_out_0[3]),
    .out_4(demultiplexer_1_out_0[4]), .out_5(demultiplexer_1_out_0[5]), .out_6(demultiplexer_1_out_0[6]),
    .out_7(demultiplexer_1_out_0[7]));
  not not_2 (full, fill_8_1_v);
  assign and_6_out = clr_8 & not_3_out;  // And and_6, 8 bits wide
  assign not_3_out = ~fill_8_1_out1;  // Not not_3, 8 bits wide
  or or_3 (or_3_out, UFL, USC);
  Multiplexer #(.Bits(5)) multiplexer_3 (
    .sel(URA), .in_0(5'b10000), .in_1(inst_wfile_1_r_a), .out({multiplexer_3_out_2[0], multiplexer_3_out}));
  Multiplexer #(.Bits(5)) multiplexer_4 (
    .sel(URB), .in_0(5'b10000), .in_1(inst_wfile_1_r_b), .out({multiplexer_3_out_2[1], multiplexer_4_out}));
  Multiplexer #(.Bits(5)) multiplexer_5 (
    .sel(or_3_out), .in_0(5'b10000), .in_1(multiplexer_6_out),
    .out({multiplexer_3_out_2[2], multiplexer_5_out}));
  Multiplexer #(.Bits(5)) multiplexer_6 (.sel(UFL), .in_0(SC), .in_1(FL), .out(multiplexer_6_out));
  assign {or_4_out_2[7], or_4_out} = demultiplexer_1_out_0 | clr_8;  // Or or_4, 8 bits wide
  assign or_5_out = fill_8_1_out1 | demultiplexer_1_out_0 | and_6_out;  // Or or_5, 8 bits wide
  assign or_6_out = multiplexer_3_out_2 | and_10_out | and_9_out;  // Or or_6, 3 bits wide
  Comparator #(.Bits(4)) comparator_5 (.a(com1_inst), .b(multiplexer_3_out), .eq(comparator_5_eq[0]));  // open: gt, lt
  Comparator #(.Bits(4)) comparator_6 (.a(com1_inst), .b(multiplexer_4_out), .eq(comparator_5_eq[1]));  // open: gt, lt
  Comparator #(.Bits(4)) comparator_7 (.a(com1_inst), .b(multiplexer_5_out), .eq(comparator_5_eq[2]));  // open: gt, lt
  Comparator #(.Bits(4)) comparator_8 (.a(com2_inst), .b(multiplexer_3_out), .eq(comparator_8_eq[0]));  // open: gt, lt
  Comparator #(.Bits(4)) comparator_9 (.a(com2_inst), .b(multiplexer_4_out), .eq(comparator_8_eq[1]));  // open: gt, lt
  Comparator #(.Bits(4)) comparator_10 (.a(com2_inst), .b(multiplexer_5_out), .eq(comparator_8_eq[2]));  // open: gt, lt
  Multiplexer multiplexer_7 (
    .sel(fill_8_1_out1[7]), .in_0(or_4_out_2[7]), .in_1(or_4_out[7]), .out(multiplexer_7_out[7]));
  Multiplexer multiplexer_8 (
    .sel(fill_8_1_out1[6]), .in_0(or_4_out[7]), .in_1(or_4_out[6]), .out(multiplexer_7_out[6]));
  Multiplexer multiplexer_9 (
    .sel(fill_8_1_out1[5]), .in_0(or_4_out[6]), .in_1(or_4_out[5]), .out(multiplexer_7_out[5]));
  Multiplexer multiplexer_10 (
    .sel(fill_8_1_out1[4]), .in_0(or_4_out[5]), .in_1(or_4_out[4]), .out(multiplexer_7_out[4]));
  Multiplexer multiplexer_11 (
    .sel(fill_8_1_out1[3]), .in_0(or_4_out[4]), .in_1(or_4_out[3]), .out(multiplexer_7_out[3]));
  Multiplexer multiplexer_12 (
    .sel(fill_8_1_out1[2]), .in_0(or_4_out[3]), .in_1(or_4_out[2]), .out(multiplexer_7_out[2]));
  Multiplexer multiplexer_13 (
    .sel(fill_8_1_out1[1]), .in_0(or_4_out[2]), .in_1(or_4_out[1]), .out(multiplexer_7_out[1]));
  Multiplexer multiplexer_14 (.sel(fill_8_1_out1[0]), .in_0(or_4_out[1]), .in_1(1'b0), .out(multiplexer_7_out[0]));
  assign not_4_out = ~multiplexer_7_out;  // Not not_4, 8 bits wide
  and and_7 (and_7_out, not_4_out[0], E);
  Multiplexer #(.Bits(3)) multiplexer_15 (
    .sel(or_5_out[0]), .in_0(or_7_out), .in_1(or_6_out), .out(multiplexer_15_out));
  assign and_8_out = bitextender_1_out & ~or_6_out;  // And and_8, 3 bits wide
  BitExtender #(.inputBits(1), .outputBits(3)) bitextender_1 (.in(or_5_out[0]), .out(bitextender_1_out));
  assign and_9_out = bitextender_2_out & comparator_5_eq;  // And and_9, 3 bits wide
  BitExtender #(.inputBits(1), .outputBits(3)) bitextender_2 (.in(com1), .out(bitextender_2_out));
  BitExtender #(.inputBits(1), .outputBits(3)) bitextender_3 (.in(com2), .out(bitextender_3_out));
  assign and_10_out = bitextender_3_out & comparator_8_eq;  // And and_10, 3 bits wide
  Register register_1 (.D(and_7_out), .C(C), .en(or_5_out[0]), .Q(register_22_q[0]));
  RS_FF rs_ff_1 (.S(multiplexer_15_out[0]), .C(C), .R(and_8_out[0]), .Q(rs_ff_1_q[0]));  // open: nQ
  RS_FF rs_ff_2 (.S(multiplexer_15_out[1]), .C(C), .R(and_8_out[1]), .Q(rs_ff_1_q[1]));  // open: nQ
  RS_FF rs_ff_3 (.S(multiplexer_15_out[2]), .C(C), .R(and_8_out[2]), .Q(rs_ff_1_q[2]));  // open: nQ
  Comparator #(.Bits(4)) comparator_11 (
    .a(com1_inst), .b(register_2_q_3[14:11]), .eq(comparator_11_eq[0]));  // open: gt, lt
  Comparator #(.Bits(4)) comparator_12 (
    .a(com1_inst), .b(register_2_q_3[10:7]), .eq(comparator_11_eq[1]));  // open: gt, lt
  Comparator #(.Bits(4)) comparator_13 (
    .a(com1_inst), .b(register_2_q_3[6:3]), .eq(comparator_11_eq[2]));  // open: gt, lt
  Comparator #(.Bits(4)) comparator_14 (
    .a(com2_inst), .b(register_2_q_3[14:11]), .eq(comparator_14_eq[0]));  // open: gt, lt
  Comparator #(.Bits(4)) comparator_15 (
    .a(com2_inst), .b(register_2_q_3[10:7]), .eq(comparator_14_eq[1]));  // open: gt, lt
  Comparator #(.Bits(4)) comparator_16 (
    .a(com2_inst), .b(register_2_q_3[6:3]), .eq(comparator_14_eq[2]));  // open: gt, lt
  Register #(.Bits(20)) register_2 (
    .D({multiplexer_3_out, multiplexer_4_out, multiplexer_5_out, UFU, ep_I, inst}), .C(C), .en(or_5_out[0]),
    .Q({register_2_q_3, register_2_q_2[4], register_2_q}));
  Register #(.Bits(32)) register_3 (.D(D), .C(C), .en(or_5_out[0]), .Q(register_3_q));
  assign not_5_out = ~clr_8;  // Not not_5, 8 bits wide
  and and_11 (and_47_out[0], register_22_q[0], bitselector_1_out, rs_ff_1_q[2], rs_ff_1_q[1], rs_ff_1_q[0]);
  assign or_7_out = and_15_out | and_14_out;  // Or or_7, 3 bits wide
  BitSelector #(.Selector_Bits(3)) bitselector_1 (.in(FU_free), .sel(register_2_q_3[2:0]), .out(bitselector_1_out));
  priority_test8 priority_test8_1 (
    .test(not_5_out), .in1(and_47_out[0]), .in2(and_47_out[1]), .in3(and_47_out[2]), .in4(and_47_out[3]),
    .in5(and_47_out[4]), .in6(and_47_out[5]), .in7(and_47_out[6]), .in8(and_47_out[7]),
    .out1(priority_test8_1_out1), .out2(priority_test8_1_out2), .out3(priority_test8_1_out3),
    .out4(priority_test8_1_out4), .out5(priority_test8_1_out5), .out6(priority_test8_1_out6),
    .out7(priority_test8_1_out7), .out8(priority_test8_1_out8));  // open: v
  PriorityEncoder #(.Selector_Bits(3)) priorityencoder_1 (
    .in0(and_47_out[0]), .in1(and_47_out[1]), .in2(and_47_out[2]), .in3(and_47_out[3]), .in4(and_47_out[4]),
    .in5(and_47_out[5]), .in6(and_47_out[6]), .in7(and_47_out[7]), .num(priorityencoder_1_num),
    .any(priorityencoder_1_any));
  and and_12 (and_12_out, not_4_out[1], register_22_q[0]);
  Multiplexer #(.Bits(3)) multiplexer_16 (
    .sel(or_5_out[1]), .in_0(or_10_out), .in_1(or_8_out), .out(multiplexer_16_out));
  assign or_8_out = or_7_out | rs_ff_1_q;  // Or or_8, 3 bits wide
  assign and_13_out = bitextender_4_out & ~or_8_out;  // And and_13, 3 bits wide
  BitExtender #(.inputBits(1), .outputBits(3)) bitextender_4 (.in(or_5_out[1]), .out(bitextender_4_out));
  assign and_14_out = bitextender_5_out & comparator_11_eq;  // And and_14, 3 bits wide
  BitExtender #(.inputBits(1), .outputBits(3)) bitextender_5 (.in(com1), .out(bitextender_5_out));
  BitExtender #(.inputBits(1), .outputBits(3)) bitextender_6 (.in(com2), .out(bitextender_6_out));
  assign and_15_out = bitextender_6_out & comparator_14_eq;  // And and_15, 3 bits wide
  inst_comp inst_comp_1 (
    .A_id(register_2_q), .A_ep(register_2_q_2[4]), .B_id(clr_id), .B_ep(clr_ep), .A_old(inst_comp_8_a_old[0]));
  BitExtender #(.inputBits(1), .outputBits(8)) bitextender_7 (.in(clr), .out(bitextender_7_out));
  or or_9 (V, priority_test8_1_out1, priority_test8_1_out2, priority_test8_1_out3, priority_test8_1_out4, priority_test8_1_out5, priority_test8_1_out6, priority_test8_1_out7, priority_test8_1_out8);
  Register register_4 (.D(and_12_out), .C(C), .en(or_5_out[1]), .Q(register_22_q[1]));
  Register #(.Bits(20)) register_5 (
    .D({register_2_q_3, register_2_q_2[4], register_2_q}), .C(C), .en(or_5_out[1]),
    .Q({register_5_q_3, register_5_q_2[4], register_5_q}));
  Register #(.Bits(32)) register_6 (.D(register_3_q), .C(C), .en(or_5_out[1]), .Q(register_6_q));
  assign and_16_out = inst_comp_8_a_old & bitextender_7_out;  // And and_16, 8 bits wide
  and and_17 (and_47_out[1], register_22_q[1], bitselector_2_out, rs_ff_4_q[2], rs_ff_4_q[1], rs_ff_4_q[0]);
  RS_FF rs_ff_4 (.S(multiplexer_16_out[0]), .C(C), .R(and_13_out[0]), .Q(rs_ff_4_q[0]));  // open: nQ
  RS_FF rs_ff_5 (.S(multiplexer_16_out[1]), .C(C), .R(and_13_out[1]), .Q(rs_ff_4_q[1]));  // open: nQ
  RS_FF rs_ff_6 (.S(multiplexer_16_out[2]), .C(C), .R(and_13_out[2]), .Q(rs_ff_4_q[2]));  // open: nQ
  assign or_10_out = and_19_out | and_18_out;  // Or or_10, 3 bits wide
  Comparator #(.Bits(4)) comparator_17 (
    .a(com1_inst), .b(register_5_q_3[14:11]), .eq(comparator_17_eq[0]));  // open: gt, lt
  Comparator #(.Bits(4)) comparator_18 (
    .a(com1_inst), .b(register_5_q_3[10:7]), .eq(comparator_17_eq[1]));  // open: gt, lt
  Comparator #(.Bits(4)) comparator_19 (
    .a(com1_inst), .b(register_5_q_3[6:3]), .eq(comparator_17_eq[2]));  // open: gt, lt
  Comparator #(.Bits(4)) comparator_20 (
    .a(com2_inst), .b(register_5_q_3[14:11]), .eq(comparator_20_eq[0]));  // open: gt, lt
  Comparator #(.Bits(4)) comparator_21 (
    .a(com2_inst), .b(register_5_q_3[10:7]), .eq(comparator_20_eq[1]));  // open: gt, lt
  Comparator #(.Bits(4)) comparator_22 (
    .a(com2_inst), .b(register_5_q_3[6:3]), .eq(comparator_20_eq[2]));  // open: gt, lt
  BitSelector #(.Selector_Bits(3)) bitselector_2 (.in(FU_free), .sel(register_5_q_3[2:0]), .out(bitselector_2_out));
  BitExtender #(.inputBits(1), .outputBits(8)) bitextender_8 (.in(res), .out(bitextender_8_out));
  assign or_11_out = or_10_out | rs_ff_4_q;  // Or or_11, 3 bits wide
  assign and_18_out = bitextender_9_out & comparator_17_eq;  // And and_18, 3 bits wide
  BitExtender #(.inputBits(1), .outputBits(3)) bitextender_9 (.in(com1), .out(bitextender_9_out));
  BitExtender #(.inputBits(1), .outputBits(3)) bitextender_10 (.in(com2), .out(bitextender_10_out));
  assign and_19_out = bitextender_10_out & comparator_20_eq;  // And and_19, 3 bits wide
  inst_comp inst_comp_2 (
    .A_id(register_5_q), .A_ep(register_5_q_2[4]), .B_id(clr_id), .B_ep(clr_ep), .A_old(inst_comp_8_a_old[1]));
  assign clr_8 = and_16_out | bitextender_8_out;  // Or or_12, 8 bits wide
  and and_20 (and_20_out, not_4_out[2], register_22_q[1]);
  Register register_7 (.D(and_20_out), .C(C), .en(or_5_out[2]), .Q(register_22_q[2]));
  Multiplexer #(.Bits(3)) multiplexer_17 (
    .sel(or_5_out[2]), .in_0(or_13_out), .in_1(or_11_out), .out(multiplexer_17_out));
  assign and_21_out = bitextender_11_out & ~or_11_out;  // And and_21, 3 bits wide
  BitExtender #(.inputBits(1), .outputBits(3)) bitextender_11 (.in(or_5_out[2]), .out(bitextender_11_out));
  Register #(.Bits(20)) register_8 (
    .D({register_5_q_3, register_5_q_2[4], register_5_q}), .C(C), .en(or_5_out[2]),
    .Q({register_8_q_3, register_8_q_2[4], register_8_q}));
  Register #(.Bits(32)) register_9 (.D(register_6_q), .C(C), .en(or_5_out[2]), .Q(register_9_q));
  and and_22 (and_47_out[2], register_22_q[2], bitselector_3_out, rs_ff_7_q[2], rs_ff_7_q[1], rs_ff_7_q[0]);
  RS_FF rs_ff_7 (.S(multiplexer_17_out[0]), .C(C), .R(and_21_out[0]), .Q(rs_ff_7_q[0]));  // open: nQ
  RS_FF rs_ff_8 (.S(multiplexer_17_out[1]), .C(C), .R(and_21_out[1]), .Q(rs_ff_7_q[1]));  // open: nQ
  RS_FF rs_ff_9 (.S(multiplexer_17_out[2]), .C(C), .R(and_21_out[2]), .Q(rs_ff_7_q[2]));  // open: nQ
  assign or_13_out = and_26_out | and_25_out;  // Or or_13, 3 bits wide
  Comparator #(.Bits(4)) comparator_23 (
    .a(com1_inst), .b(register_8_q_3[14:11]), .eq(comparator_23_eq[0]));  // open: gt, lt
  Comparator #(.Bits(4)) comparator_24 (
    .a(com1_inst), .b(register_8_q_3[10:7]), .eq(comparator_23_eq[1]));  // open: gt, lt
  Comparator #(.Bits(4)) comparator_25 (
    .a(com1_inst), .b(register_8_q_3[6:3]), .eq(comparator_23_eq[2]));  // open: gt, lt
  Comparator #(.Bits(4)) comparator_26 (
    .a(com2_inst), .b(register_8_q_3[14:11]), .eq(comparator_26_eq[0]));  // open: gt, lt
  Comparator #(.Bits(4)) comparator_27 (
    .a(com2_inst), .b(register_8_q_3[10:7]), .eq(comparator_26_eq[1]));  // open: gt, lt
  Comparator #(.Bits(4)) comparator_28 (
    .a(com2_inst), .b(register_8_q_3[6:3]), .eq(comparator_26_eq[2]));  // open: gt, lt
  BitSelector #(.Selector_Bits(3)) bitselector_3 (.in(FU_free), .sel(register_8_q_3[2:0]), .out(bitselector_3_out));
  assign or_14_out = or_13_out | rs_ff_7_q;  // Or or_14, 3 bits wide
  inst_comp inst_comp_3 (
    .A_id(register_8_q), .A_ep(register_8_q_2[4]), .B_id(clr_id), .B_ep(clr_ep), .A_old(inst_comp_8_a_old[2]));
  and and_23 (and_23_out, not_4_out[3], register_22_q[2]);
  Register register_10 (.D(and_23_out), .C(C), .en(or_5_out[3]), .Q(register_22_q[3]));
  Multiplexer #(.Bits(3)) multiplexer_18 (
    .sel(or_5_out[3]), .in_0(or_15_out), .in_1(or_14_out), .out(multiplexer_18_out));
  assign and_24_out = bitextender_12_out & ~or_14_out;  // And and_24, 3 bits wide
  BitExtender #(.inputBits(1), .outputBits(3)) bitextender_12 (.in(or_5_out[3]), .out(bitextender_12_out));
  assign and_25_out = bitextender_13_out & comparator_23_eq;  // And and_25, 3 bits wide
  BitExtender #(.inputBits(1), .outputBits(3)) bitextender_13 (.in(com1), .out(bitextender_13_out));
  BitExtender #(.inputBits(1), .outputBits(3)) bitextender_14 (.in(com2), .out(bitextender_14_out));
  assign and_26_out = bitextender_14_out & comparator_26_eq;  // And and_26, 3 bits wide
  RS_FF rs_ff_10 (.S(multiplexer_18_out[0]), .C(C), .R(and_24_out[0]), .Q(rs_ff_10_q[0]));  // open: nQ
  RS_FF rs_ff_11 (.S(multiplexer_18_out[1]), .C(C), .R(and_24_out[1]), .Q(rs_ff_10_q[1]));  // open: nQ
  RS_FF rs_ff_12 (.S(multiplexer_18_out[2]), .C(C), .R(and_24_out[2]), .Q(rs_ff_10_q[2]));  // open: nQ
  assign or_15_out = and_31_out | and_30_out;  // Or or_15, 3 bits wide
  Comparator #(.Bits(4)) comparator_29 (
    .a(com1_inst), .b(register_11_q_3[14:11]), .eq(comparator_29_eq[0]));  // open: gt, lt
  Comparator #(.Bits(4)) comparator_30 (
    .a(com1_inst), .b(register_11_q_3[10:7]), .eq(comparator_29_eq[1]));  // open: gt, lt
  Comparator #(.Bits(4)) comparator_31 (
    .a(com1_inst), .b(register_11_q_3[6:3]), .eq(comparator_29_eq[2]));  // open: gt, lt
  Comparator #(.Bits(4)) comparator_32 (
    .a(com2_inst), .b(register_11_q_3[14:11]), .eq(comparator_32_eq[0]));  // open: gt, lt
  Comparator #(.Bits(4)) comparator_33 (
    .a(com2_inst), .b(register_11_q_3[10:7]), .eq(comparator_32_eq[1]));  // open: gt, lt
  Comparator #(.Bits(4)) comparator_34 (
    .a(com2_inst), .b(register_11_q_3[6:3]), .eq(comparator_32_eq[2]));  // open: gt, lt
  BitSelector #(.Selector_Bits(3)) bitselector_4 (.in(FU_free), .sel(register_11_q_3[2:0]), .out(bitselector_4_out));
  Register #(.Bits(20)) register_11 (
    .D({register_8_q_3, register_8_q_2[4], register_8_q}), .C(C), .en(or_5_out[3]),
    .Q({register_11_q_3, register_11_q_2[4], register_11_q}));
  Register #(.Bits(32)) register_12 (.D(register_9_q), .C(C), .en(or_5_out[3]), .Q(register_12_q));
  and and_27 (and_47_out[3], register_22_q[3], bitselector_4_out, rs_ff_10_q[2], rs_ff_10_q[1], rs_ff_10_q[0]);
  and and_28 (and_28_out, not_4_out[4], register_22_q[3]);
  Multiplexer #(.Bits(3)) multiplexer_19 (
    .sel(or_5_out[4]), .in_0(or_17_out), .in_1(or_16_out), .out(multiplexer_19_out));
  assign or_16_out = or_15_out | rs_ff_10_q;  // Or or_16, 3 bits wide
  assign and_29_out = bitextender_15_out & ~or_16_out;  // And and_29, 3 bits wide
  BitExtender #(.inputBits(1), .outputBits(3)) bitextender_15 (.in(or_5_out[4]), .out(bitextender_15_out));
  assign and_30_out = bitextender_16_out & comparator_29_eq;  // And and_30, 3 bits wide
  BitExtender #(.inputBits(1), .outputBits(3)) bitextender_16 (.in(com1), .out(bitextender_16_out));
  BitExtender #(.inputBits(1), .outputBits(3)) bitextender_17 (.in(com2), .out(bitextender_17_out));
  assign and_31_out = bitextender_17_out & comparator_32_eq;  // And and_31, 3 bits wide
  inst_comp inst_comp_4 (
    .A_id(register_11_q), .A_ep(register_11_q_2[4]), .B_id(clr_id), .B_ep(clr_ep),
    .A_old(inst_comp_8_a_old[3]));
  Register register_13 (.D(and_28_out), .C(C), .en(or_5_out[4]), .Q(register_22_q[4]));
  RS_FF rs_ff_13 (.S(multiplexer_19_out[0]), .C(C), .R(and_29_out[0]), .Q(rs_ff_13_q[0]));  // open: nQ
  RS_FF rs_ff_14 (.S(multiplexer_19_out[1]), .C(C), .R(and_29_out[1]), .Q(rs_ff_13_q[1]));  // open: nQ
  RS_FF rs_ff_15 (.S(multiplexer_19_out[2]), .C(C), .R(and_29_out[2]), .Q(rs_ff_13_q[2]));  // open: nQ
  Comparator #(.Bits(4)) comparator_35 (
    .a(com1_inst), .b(register_14_q_3[14:11]), .eq(comparator_35_eq[0]));  // open: gt, lt
  Comparator #(.Bits(4)) comparator_36 (
    .a(com1_inst), .b(register_14_q_3[10:7]), .eq(comparator_35_eq[1]));  // open: gt, lt
  Comparator #(.Bits(4)) comparator_37 (
    .a(com1_inst), .b(register_14_q_3[6:3]), .eq(comparator_35_eq[2]));  // open: gt, lt
  Comparator #(.Bits(4)) comparator_38 (
    .a(com2_inst), .b(register_14_q_3[14:11]), .eq(comparator_38_eq[0]));  // open: gt, lt
  Comparator #(.Bits(4)) comparator_39 (
    .a(com2_inst), .b(register_14_q_3[10:7]), .eq(comparator_38_eq[1]));  // open: gt, lt
  Comparator #(.Bits(4)) comparator_40 (
    .a(com2_inst), .b(register_14_q_3[6:3]), .eq(comparator_38_eq[2]));  // open: gt, lt
  Register #(.Bits(20)) register_14 (
    .D({register_11_q_3, register_11_q_2[4], register_11_q}), .C(C), .en(or_5_out[4]),
    .Q({register_14_q_3, register_14_q_2[4], register_14_q}));
  Register #(.Bits(32)) register_15 (.D(register_12_q), .C(C), .en(or_5_out[4]), .Q(register_15_q));
  and and_32 (and_47_out[4], register_22_q[4], bitselector_5_out, rs_ff_13_q[2], rs_ff_13_q[1], rs_ff_13_q[0]);
  assign or_17_out = and_36_out | and_35_out;  // Or or_17, 3 bits wide
  BitSelector #(.Selector_Bits(3)) bitselector_5 (.in(FU_free), .sel(register_14_q_3[2:0]), .out(bitselector_5_out));
  and and_33 (and_33_out, not_4_out[5], register_22_q[4]);
  Multiplexer #(.Bits(3)) multiplexer_20 (
    .sel(or_5_out[5]), .in_0(or_19_out), .in_1(or_18_out), .out(multiplexer_20_out));
  assign or_18_out = or_17_out | rs_ff_13_q;  // Or or_18, 3 bits wide
  assign and_34_out = bitextender_18_out & ~or_18_out;  // And and_34, 3 bits wide
  BitExtender #(.inputBits(1), .outputBits(3)) bitextender_18 (.in(or_5_out[5]), .out(bitextender_18_out));
  assign and_35_out = bitextender_19_out & comparator_35_eq;  // And and_35, 3 bits wide
  BitExtender #(.inputBits(1), .outputBits(3)) bitextender_19 (.in(com1), .out(bitextender_19_out));
  BitExtender #(.inputBits(1), .outputBits(3)) bitextender_20 (.in(com2), .out(bitextender_20_out));
  assign and_36_out = bitextender_20_out & comparator_38_eq;  // And and_36, 3 bits wide
  inst_comp inst_comp_5 (
    .A_id(register_14_q), .A_ep(register_14_q_2[4]), .B_id(clr_id), .B_ep(clr_ep),
    .A_old(inst_comp_8_a_old[4]));
  Register register_16 (.D(and_33_out), .C(C), .en(or_5_out[5]), .Q(register_22_q[5]));
  Register #(.Bits(20)) register_17 (
    .D({register_14_q_3, register_14_q_2[4], register_14_q}), .C(C), .en(or_5_out[5]),
    .Q({register_17_q[19:8], register_17_q_2, register_17_q[4:0]}));
  Register #(.Bits(32)) register_18 (.D(register_15_q), .C(C), .en(or_5_out[5]), .Q(register_18_q));
  and and_37 (and_47_out[5], register_22_q[5], bitselector_6_out, rs_ff_16_q[2], rs_ff_16_q[1], rs_ff_16_q[0]);
  RS_FF rs_ff_16 (.S(multiplexer_20_out[0]), .C(C), .R(and_34_out[0]), .Q(rs_ff_16_q[0]));  // open: nQ
  RS_FF rs_ff_17 (.S(multiplexer_20_out[1]), .C(C), .R(and_34_out[1]), .Q(rs_ff_16_q[1]));  // open: nQ
  RS_FF rs_ff_18 (.S(multiplexer_20_out[2]), .C(C), .R(and_34_out[2]), .Q(rs_ff_16_q[2]));  // open: nQ
  assign or_19_out = and_39_out | and_38_out;  // Or or_19, 3 bits wide
  Comparator #(.Bits(4)) comparator_41 (
    .a(com1_inst), .b(register_17_q[19:16]), .eq(comparator_41_eq[0]));  // open: gt, lt
  Comparator #(.Bits(4)) comparator_42 (
    .a(com1_inst), .b(register_17_q[15:12]), .eq(comparator_41_eq[1]));  // open: gt, lt
  Comparator #(.Bits(4)) comparator_43 (
    .a(com1_inst), .b(register_17_q[11:8]), .eq(comparator_41_eq[2]));  // open: gt, lt
  Comparator #(.Bits(4)) comparator_44 (
    .a(com2_inst), .b(register_17_q[19:16]), .eq(comparator_44_eq[0]));  // open: gt, lt
  Comparator #(.Bits(4)) comparator_45 (
    .a(com2_inst), .b(register_17_q[15:12]), .eq(comparator_44_eq[1]));  // open: gt, lt
  Comparator #(.Bits(4)) comparator_46 (
    .a(com2_inst), .b(register_17_q[11:8]), .eq(comparator_44_eq[2]));  // open: gt, lt
  BitSelector #(.Selector_Bits(3)) bitselector_6 (.in(FU_free), .sel(register_17_q_2), .out(bitselector_6_out));
  assign or_20_out = or_19_out | rs_ff_16_q;  // Or or_20, 3 bits wide
  assign and_38_out = bitextender_21_out & comparator_41_eq;  // And and_38, 3 bits wide
  BitExtender #(.inputBits(1), .outputBits(3)) bitextender_21 (.in(com1), .out(bitextender_21_out));
  BitExtender #(.inputBits(1), .outputBits(3)) bitextender_22 (.in(com2), .out(bitextender_22_out));
  assign and_39_out = bitextender_22_out & comparator_44_eq;  // And and_39, 3 bits wide
  inst_comp inst_comp_6 (
    .A_id(register_17_q[3:0]), .A_ep(register_17_q[4]), .B_id(clr_id), .B_ep(clr_ep),
    .A_old(inst_comp_8_a_old[5]));
  and and_40 (and_40_out, not_4_out[6], register_22_q[5]);
  Register register_19 (.D(and_40_out), .C(C), .en(or_5_out[6]), .Q(register_22_q[6]));
  Multiplexer #(.Bits(3)) multiplexer_21 (
    .sel(or_5_out[6]), .in_0(or_21_out), .in_1(or_20_out), .out(multiplexer_21_out));
  assign and_41_out = bitextender_23_out & ~or_20_out;  // And and_41, 3 bits wide
  BitExtender #(.inputBits(1), .outputBits(3)) bitextender_23 (.in(or_5_out[6]), .out(bitextender_23_out));
  Register #(.Bits(20)) register_20 (
    .D({register_17_q[19:8], register_17_q_2, register_17_q[4:0]}), .C(C), .en(or_5_out[6]),
    .Q({register_20_q_3, register_20_q_2[4], register_20_q}));
  Register #(.Bits(32)) register_21 (.D(register_18_q), .C(C), .en(or_5_out[6]), .Q(register_21_q));
  and and_42 (and_47_out[6], register_22_q[6], bitselector_7_out, rs_ff_19_q[2], rs_ff_19_q[1], rs_ff_19_q[0]);
  RS_FF rs_ff_19 (.S(multiplexer_21_out[0]), .C(C), .R(and_41_out[0]), .Q(rs_ff_19_q[0]));  // open: nQ
  RS_FF rs_ff_20 (.S(multiplexer_21_out[1]), .C(C), .R(and_41_out[1]), .Q(rs_ff_19_q[1]));  // open: nQ
  RS_FF rs_ff_21 (.S(multiplexer_21_out[2]), .C(C), .R(and_41_out[2]), .Q(rs_ff_19_q[2]));  // open: nQ
  assign or_21_out = and_46_out | and_45_out;  // Or or_21, 3 bits wide
  Comparator #(.Bits(4)) comparator_47 (
    .a(com1_inst), .b(register_20_q_3[14:11]), .eq(comparator_47_eq[0]));  // open: gt, lt
  Comparator #(.Bits(4)) comparator_48 (
    .a(com1_inst), .b(register_20_q_3[10:7]), .eq(comparator_47_eq[1]));  // open: gt, lt
  Comparator #(.Bits(4)) comparator_49 (
    .a(com1_inst), .b(register_20_q_3[6:3]), .eq(comparator_47_eq[2]));  // open: gt, lt
  Comparator #(.Bits(4)) comparator_50 (
    .a(com2_inst), .b(register_20_q_3[14:11]), .eq(comparator_50_eq[0]));  // open: gt, lt
  Comparator #(.Bits(4)) comparator_51 (
    .a(com2_inst), .b(register_20_q_3[10:7]), .eq(comparator_50_eq[1]));  // open: gt, lt
  Comparator #(.Bits(4)) comparator_52 (
    .a(com2_inst), .b(register_20_q_3[6:3]), .eq(comparator_50_eq[2]));  // open: gt, lt
  BitSelector #(.Selector_Bits(3)) bitselector_7 (.in(FU_free), .sel(register_20_q_3[2:0]), .out(bitselector_7_out));
  assign or_22_out = or_21_out | rs_ff_19_q;  // Or or_22, 3 bits wide
  inst_comp inst_comp_7 (
    .A_id(register_20_q), .A_ep(register_20_q_2[4]), .B_id(clr_id), .B_ep(clr_ep),
    .A_old(inst_comp_8_a_old[6]));
  and and_43 (and_43_out, not_4_out[7], register_22_q[6]);
  Register register_22 (.D(and_43_out), .C(C), .en(or_5_out[7]), .Q(register_22_q[7]));
  Multiplexer #(.Bits(3)) multiplexer_22 (
    .sel(or_5_out[7]), .in_0(or_23_out), .in_1(or_22_out), .out(multiplexer_22_out));
  assign and_44_out = bitextender_24_out & ~or_22_out;  // And and_44, 3 bits wide
  BitExtender #(.inputBits(1), .outputBits(3)) bitextender_24 (.in(or_5_out[7]), .out(bitextender_24_out));
  assign and_45_out = bitextender_25_out & comparator_47_eq;  // And and_45, 3 bits wide
  BitExtender #(.inputBits(1), .outputBits(3)) bitextender_25 (.in(com1), .out(bitextender_25_out));
  BitExtender #(.inputBits(1), .outputBits(3)) bitextender_26 (.in(com2), .out(bitextender_26_out));
  assign and_46_out = bitextender_26_out & comparator_50_eq;  // And and_46, 3 bits wide
  RS_FF rs_ff_22 (.S(multiplexer_22_out[0]), .C(C), .R(and_44_out[0]), .Q(rs_ff_22_q[0]));  // open: nQ
  RS_FF rs_ff_23 (.S(multiplexer_22_out[1]), .C(C), .R(and_44_out[1]), .Q(rs_ff_22_q[1]));  // open: nQ
  RS_FF rs_ff_24 (.S(multiplexer_22_out[2]), .C(C), .R(and_44_out[2]), .Q(rs_ff_22_q[2]));  // open: nQ
  assign or_23_out = and_49_out | and_48_out;  // Or or_23, 3 bits wide
  Comparator #(.Bits(4)) comparator_53 (
    .a(com1_inst), .b(register_23_q_3[14:11]), .eq(comparator_53_eq[0]));  // open: gt, lt
  Comparator #(.Bits(4)) comparator_54 (
    .a(com1_inst), .b(register_23_q_3[10:7]), .eq(comparator_53_eq[1]));  // open: gt, lt
  Comparator #(.Bits(4)) comparator_55 (
    .a(com1_inst), .b(register_23_q_3[6:3]), .eq(comparator_53_eq[2]));  // open: gt, lt
  Comparator #(.Bits(4)) comparator_56 (
    .a(com2_inst), .b(register_23_q_3[14:11]), .eq(comparator_56_eq[0]));  // open: gt, lt
  Comparator #(.Bits(4)) comparator_57 (
    .a(com2_inst), .b(register_23_q_3[10:7]), .eq(comparator_56_eq[1]));  // open: gt, lt
  Comparator #(.Bits(4)) comparator_58 (
    .a(com2_inst), .b(register_23_q_3[6:3]), .eq(comparator_56_eq[2]));  // open: gt, lt
  BitSelector #(.Selector_Bits(3)) bitselector_8 (.in(FU_free), .sel(register_23_q_3[2:0]), .out(bitselector_8_out));
  Register #(.Bits(20)) register_23 (
    .D({register_20_q_3, register_20_q_2[4], register_20_q}), .C(C), .en(or_5_out[7]),
    .Q({register_23_q_3, register_23_q_2[4], register_23_q}));
  Register #(.Bits(32)) register_24 (.D(register_21_q), .C(C), .en(or_5_out[7]), .Q(register_24_q));
  and and_47 (and_47_out[7], register_22_q[7], bitselector_8_out, rs_ff_22_q[2], rs_ff_22_q[1], rs_ff_22_q[0]);
  assign or_24_out = or_23_out | rs_ff_22_q;  // Or or_24, 3 bits wide
  assign and_48_out = bitextender_27_out & comparator_53_eq;  // And and_48, 3 bits wide
  BitExtender #(.inputBits(1), .outputBits(3)) bitextender_27 (.in(com1), .out(bitextender_27_out));
  BitExtender #(.inputBits(1), .outputBits(3)) bitextender_28 (.in(com2), .out(bitextender_28_out));
  assign and_49_out = bitextender_28_out & comparator_56_eq;  // And and_49, 3 bits wide
  Multiplexer #(.Selector_Bits(3), .Bits(5)) multiplexer_23 (
    .sel(priorityencoder_1_num), .in_0({register_2_q_2[4], register_2_q}),
    .in_1({register_5_q_2[4], register_5_q}), .in_2({register_8_q_2[4], register_8_q}),
    .in_3({register_11_q_2[4], register_11_q}), .in_4({register_14_q_2[4], register_14_q}),
    .in_5(register_17_q[4:0]), .in_6({register_20_q_2[4], register_20_q}),
    .in_7({register_23_q_2[4], register_23_q}), .out({ep_O, disp}));
  Multiplexer #(.Selector_Bits(3), .Bits(32)) multiplexer_24 (
    .sel(priorityencoder_1_num), .in_0(register_3_q), .in_1(register_6_q), .in_2(register_9_q),
    .in_3(register_12_q), .in_4(register_15_q), .in_5(register_18_q), .in_6(register_21_q),
    .in_7(register_24_q), .out(disp_32));
  inst_comp inst_comp_8 (
    .A_id(register_23_q), .A_ep(register_23_q_2[4]), .B_id(clr_id), .B_ep(clr_ep),
    .A_old(inst_comp_8_a_old[7]));

  // Other names for the same wires on the sheet: epoch_out = ep_O; clear = clr; epoch_in = ep_I; issue[3:0] = inst;
  //   reset = res

  // Notes on the sheet:
  //   res: reset
  //   inst: inst
  //   E: enable
  //   D: inst data
  //   ep_I: epoch
endmodule
