// Digital circuit store-buffer.dig as structural Verilog
module store_buffer (
  input  W_d,
  input  C,
  input  [31:0] D,
  input  [31:0] A,
  input  [3:0] inst,
  input  [3:0] com1_id,
  input  [3:0] com2_id,
  input  com1,
  input  com2,
  input  ld_ep,
  input  [3:0] ld_id,
  input  epoch,
  input  [31:0] ld_addr,
  input  W_id,
  input  [3:0] inst_W,
  input  LD,
  input  [1:0] MD,
  input  clr,
  input  [3:0] clr_id,
  input  clr_ep,
  output [31:0] D_O,
  output [31:0] A_O,
  output V,
  output full,
  output ld_V,
  output [31:0] ld_D,
  output [3:0] id_O,
  output ep_O,
  output [1:0] MD_O
);

  wire and_1_out, and_4_out, and_6_out, and_10_out, and_12_out, and_15_out, and_17_out, and_19_out,
       and_22_out, and_25_out, and_27_out, and_30_out, comparator_1_eq, comparator_2_eq, comparator_3_eq,
       comparator_4_eq, comparator_5_eq, comparator_6_eq, comparator_7_eq, comparator_8_eq, comparator_9_eq,
       comparator_10_eq, comparator_11_eq, comparator_12_eq, comparator_13_eq, comparator_14_eq,
       comparator_15_eq, comparator_16_eq, inst_comp_1_a_old, inst_comp_2_a_old, inst_comp_3_a_old,
       inst_comp_4_a_old, inst_comp_5_a_old, inst_comp_6_a_old, inst_comp_7_a_old, inst_comp_8_a_old, M1_CLR,
       M1_CMP, M1_COM, M1_DE, M1_epoch, M1_IE, M1_RS, M1_SEL, M1_VO, M2_CLR, M2_CMP, M2_COM, M2_DE, M2_epoch,
       M2_IE, M2_RS, M2_SEL, M2_VO, M3_CLR, M3_CMP, M3_COM, M3_DE, M3_epoch, M3_IE, M3_RS, M3_SEL, M3_VO,
       M4_CLR, M4_CMP, M4_COM, M4_DE, M4_epoch, M4_IE, M4_RS, M4_SEL, M4_VO, or_1_out, or_2_out, or_6_out,
       or_7_out, or_8_out, or_9_out, priorityencoder_2_any, V_t;
  wire [1:0] empty_id, M1_MD, M2_MD, M3_MD, M4_MD, priorityencoder_1_num, priorityencoder_3_num,
       register_1_q, register_3_q, register_6_q, register_8_q, sel_com;
  wire [3:0] and_2_out, and_5_out, and_7_out, and_8_out, and_9_out, bitextender_1_out, bitextender_2_out,
       bitextender_3_out, bitselector_1_out, bitselector_2_out, demultiplexer_2_out_0, fill_4_1_out1,
       M1_inst, M2_inst, M3_inst, M4_inst, mux1x4_1_out, not_1_out, not_2_out, not_4_out, or_3_out, or_5_out,
       priority_4_1_out1, register_2_q;
  wire [31:0] M1_A, M1_D, M2_A, M2_D, M3_A, M3_D, M4_A, M4_D;

  fill_4 fill_4_1 (
    .on(1'b0), .in1(not_1_out[0]), .in2(not_1_out[1]), .in3(not_1_out[2]), .in4(not_1_out[3]),
    .out1(fill_4_1_out1[3]), .out2(fill_4_1_out1[2]), .out3(fill_4_1_out1[1]), .out4(fill_4_1_out1[0]));  // open: v
  assign not_1_out = ~register_2_q;  // Not not_1, 4 bits wide
  or or_1 (or_1_out, M4_CLR, M3_CLR, M2_CLR, M1_CLR);
  Multiplexer #(.Selector_Bits(2), .Bits(4)) multiplexer_1 (
    .sel(sel_com), .in_0(M1_inst), .in_1(M2_inst), .in_2(M3_inst), .in_3(M4_inst), .out(id_O));
  PriorityEncoder #(.Selector_Bits(2)) priorityencoder_1 (
    .in0(M1_CMP), .in1(M2_CMP), .in2(M3_CMP), .in3(M4_CMP), .num(priorityencoder_1_num), .any(ld_V));
  Multiplexer #(.Selector_Bits(2), .Bits(32)) multiplexer_2 (
    .sel(sel_com), .in_0(M1_D), .in_1(M2_D), .in_2(M3_D), .in_3(M4_D), .out(D_O));
  or or_2 (or_2_out, LD, or_1_out);
  priority_4 priority_4_1 (
    .on(LD), .in1(and_7_out[0]), .in2(and_7_out[1]), .in3(and_7_out[2]), .in4(and_7_out[3]),
    .out1(priority_4_1_out1[3]), .out2(priority_4_1_out1[2]), .out3(priority_4_1_out1[1]),
    .out4(priority_4_1_out1[0]));  // open: v
  and and_1 (and_1_out, not_4_out[3], W_id);
  assign and_2_out = ~{M4_CLR, M3_CLR, M2_CLR, M1_CLR} & {M4_COM, M3_COM, M2_COM, M1_COM};  // And and_2, 4 bits wide
  Register #(.Bits(2)) register_1 (.D(empty_id), .C(C), .en(W_id), .Q(register_1_q));
  // Probe instM1 on M1_inst
  // Probe instM2 on M2_inst
  // Probe instM3 on M3_inst
  // Probe instM4 on M4_inst
  // Probe vM1 on M1_VO
  // Probe vM2 on M2_VO
  // Probe vM3 on M3_VO
  // Probe vM4 on M4_VO
  // Probe comM1 on M1_COM
  // Probe comM2 on M2_COM
  // Probe comM3 on M3_COM
  // Probe comM4 on M4_COM
  assign not_2_out = ~{M4_VO, M3_VO, M2_VO, M1_VO};  // Not not_2, 4 bits wide
  BitExtender #(.inputBits(1), .outputBits(4)) bitextender_1 (.in(W_d), .out(bitextender_1_out));
  Register register_2 (.D(and_1_out), .C(C), .en(or_5_out[3]), .Q(register_2_q[0]));
  BitSelector #(.Selector_Bits(2)) bitselector_1 (.in(and_2_out), .sel(register_1_q), .out(bitselector_1_out[0]));
  BitSelector #(.Selector_Bits(2)) bitselector_2 (
    .in({M4_CLR, M3_CLR, M2_CLR, M1_CLR}), .sel(register_1_q), .out(bitselector_2_out[3]));
  PriorityEncoder #(.Selector_Bits(2)) priorityencoder_2 (
    .in0(not_2_out[0]), .in1(not_2_out[1]), .in2(not_2_out[2]), .in3(not_2_out[3]), .num(empty_id),
    .any(priorityencoder_2_any));
  assign {M4_DE, M3_DE, M2_DE, M1_DE} = {M4_SEL, M3_SEL, M2_SEL, M1_SEL} & bitextender_1_out;  // And and_3, 4 bits wide
  assign or_3_out = priority_4_1_out1 | bitselector_2_out;  // Or or_3, 4 bits wide
  and and_4 (and_4_out, not_4_out[2], register_2_q[0]);
  Register #(.Bits(2)) register_3 (.D(register_1_q), .C(C), .en(W_id), .Q(register_3_q));
  Multiplexer #(.Selector_Bits(2)) multiplexer_3 (
    .sel(sel_com), .in_0(M1_epoch), .in_1(M2_epoch), .in_2(M3_epoch), .in_3(M4_epoch), .out(ep_O));
  Multiplexer #(.Selector_Bits(2), .Bits(32)) multiplexer_4 (
    .sel(priorityencoder_1_num), .in_0(M1_D), .in_1(M2_D), .in_2(M3_D), .in_3(M4_D), .out(ld_D));
  not not_3 (full, priorityencoder_2_any);
  Multiplexer #(.Selector_Bits(2), .Bits(32)) multiplexer_5 (
    .sel(sel_com), .in_0(M1_A), .in_1(M2_A), .in_2(M3_A), .in_3(M4_A), .out(A_O));
  BitExtender #(.inputBits(1), .outputBits(4)) bitextender_2 (.in(W_id), .out(bitextender_2_out));
  Register register_4 (.D(and_4_out), .C(C), .en(or_5_out[2]), .Q(register_2_q[1]));
  BitSelector #(.Selector_Bits(2)) bitselector_3 (.in(and_2_out), .sel(register_3_q), .out(bitselector_1_out[1]));
  BitSelector #(.Selector_Bits(2)) bitselector_4 (
    .in({M4_CLR, M3_CLR, M2_CLR, M1_CLR}), .sel(register_3_q), .out(bitselector_2_out[2]));
  mux1x4 mux1x4_1 (.A(or_3_out), .B({1'b0, or_3_out[3:1]}), .S(or_5_out), .out(mux1x4_1_out));
  BitExtender #(.inputBits(1), .outputBits(4)) bitextender_3 (.in(or_2_out), .out(bitextender_3_out));
  assign and_5_out = bitextender_2_out & fill_4_1_out1;  // And and_5, 4 bits wide
  and and_6 (and_6_out, not_4_out[1], register_2_q[1]);
  Register register_5 (.D(and_6_out), .C(C), .en(or_5_out[1]), .Q(register_2_q[2]));
  assign and_7_out = register_2_q & bitselector_1_out;  // And and_7, 4 bits wide
  Register #(.Bits(2)) register_6 (.D(register_3_q), .C(C), .en(W_id), .Q(register_6_q));
  Demultiplexer #(.Selector_Bits(2)) demultiplexer_1 (
    .sel(empty_id), .in(W_id), .out_0(M1_IE), .out_1(M2_IE), .out_2(M3_IE), .out_3(M4_IE));
  Demultiplexer #(.Selector_Bits(2)) demultiplexer_2 (
    .sel(sel_com), .in(V_t), .out_0(demultiplexer_2_out_0[0]), .out_1(demultiplexer_2_out_0[1]),
    .out_2(demultiplexer_2_out_0[2]), .out_3(demultiplexer_2_out_0[3]));
  assign and_8_out = mux1x4_1_out & bitextender_3_out;  // And and_8, 4 bits wide
  assign and_9_out = bitextender_3_out & or_3_out;  // And and_9, 4 bits wide
  and and_10 (and_10_out, not_4_out[0], register_2_q[2]);
  BitSelector #(.Selector_Bits(2)) bitselector_5 (.in(and_2_out), .sel(register_6_q), .out(bitselector_1_out[2]));
  BitSelector #(.Selector_Bits(2)) bitselector_6 (
    .in({M4_CLR, M3_CLR, M2_CLR, M1_CLR}), .sel(register_6_q), .out(bitselector_2_out[1]));
  Multiplexer #(.Selector_Bits(2), .Bits(2)) multiplexer_6 (
    .sel(sel_com), .in_0(M1_MD), .in_1(M2_MD), .in_2(M3_MD), .in_3(M4_MD), .out(MD_O));
  assign {M4_RS, M3_RS, M2_RS, M1_RS} = {M4_CLR, M3_CLR, M2_CLR, M1_CLR} | demultiplexer_2_out_0;  // Or or_4, 4 bits wide
  assign not_4_out = ~and_8_out;  // Not not_4, 4 bits wide
  assign or_5_out = and_9_out | and_5_out;  // Or or_5, 4 bits wide
  Register register_7 (.D(and_10_out), .C(C), .en(or_5_out[0]), .Q(register_2_q[3]));
  PriorityEncoder #(.Selector_Bits(2)) priorityencoder_3 (
    .in0(and_7_out[0]), .in1(and_7_out[1]), .in2(and_7_out[2]), .in3(and_7_out[3]),
    .num(priorityencoder_3_num), .any(V));
  BitSelector #(.Selector_Bits(2)) bitselector_7 (.in(and_2_out), .sel(register_8_q), .out(bitselector_1_out[3]));
  Register #(.Bits(2)) register_8 (.D(register_6_q), .C(C), .en(W_id), .Q(register_8_q));
  BitSelector #(.Selector_Bits(2)) bitselector_8 (
    .in({M4_CLR, M3_CLR, M2_CLR, M1_CLR}), .sel(register_8_q), .out(bitselector_2_out[0]));
  Multiplexer #(.Selector_Bits(2), .Bits(2)) multiplexer_7 (
    .sel(priorityencoder_3_num), .in_0(register_1_q), .in_1(register_3_q), .in_2(register_6_q),
    .in_3(register_8_q), .out(sel_com));
  and and_11 (V_t, V, LD);
  RS_FF rs_ff_1 (.S(M1_IE), .C(C), .R(M1_RS), .Q(M1_VO));  // open: nQ
  Comparator #(.Bits(32)) comparator_1 (.a(ld_addr), .b(M1_A), .eq(comparator_1_eq));  // open: gt, lt
  Register #(.Bits(32)) register_9 (.D(A), .C(C), .en(M1_DE), .Q(M1_A));
  Register #(.Bits(32)) register_10 (.D(D), .C(C), .en(M1_DE), .Q(M1_D));
  Register #(.Bits(2)) register_11 (.D(MD), .C(C), .en(M1_DE), .Q(M1_MD));
  Comparator #(.Bits(4)) comparator_2 (.a(M1_inst), .b(inst_W), .eq(comparator_2_eq));  // open: gt, lt
  RS_FF rs_ff_2 (.S(or_6_out), .C(C), .R(M1_RS), .Q(M1_COM));  // open: nQ
  and and_12 (and_12_out, com2, M1_VO, comparator_4_eq);
  Comparator #(.Bits(4)) comparator_3 (.a(M1_inst), .b(com1_id), .eq(comparator_3_eq));  // open: gt, lt
  Comparator #(.Bits(4)) comparator_4 (.a(M1_inst), .b(com2_id), .eq(comparator_4_eq));  // open: gt, lt
  Register #(.Bits(4)) register_12 (.D(inst), .C(C), .en(M1_IE), .Q(M1_inst));
  Register register_13 (.D(epoch), .C(C), .en(M1_IE), .Q(M1_epoch));
  inst_comp inst_comp_1 (.A_id(ld_id), .A_ep(ld_ep), .B_id(M1_inst), .B_ep(M1_epoch), .A_old(inst_comp_1_a_old));
  inst_comp inst_comp_2 (.A_id(M1_inst), .A_ep(M1_epoch), .B_id(clr_id), .B_ep(clr_ep), .A_old(inst_comp_2_a_old));
  and and_13 (M1_CMP, M1_VO, comparator_1_eq, inst_comp_1_a_old, 1'b1);
  and and_14 (M1_SEL, M1_VO, comparator_2_eq);
  or or_6 (or_6_out, and_12_out, and_15_out);
  and and_15 (and_15_out, comparator_3_eq, M1_VO, com1);
  and and_16 (M1_CLR, inst_comp_2_a_old, clr);
  and and_17 (and_17_out, com2, M2_VO, comparator_8_eq);
  RS_FF rs_ff_3 (.S(M2_IE), .C(C), .R(M2_RS), .Q(M2_VO));  // open: nQ
  Comparator #(.Bits(32)) comparator_5 (.a(ld_addr), .b(M2_A), .eq(comparator_5_eq));  // open: gt, lt
  Register #(.Bits(32)) register_14 (.D(A), .C(C), .en(M2_DE), .Q(M2_A));
  Register #(.Bits(32)) register_15 (.D(D), .C(C), .en(M2_DE), .Q(M2_D));
  Register #(.Bits(2)) register_16 (.D(MD), .C(C), .en(M2_DE), .Q(M2_MD));
  Comparator #(.Bits(4)) comparator_6 (.a(M2_inst), .b(inst_W), .eq(comparator_6_eq));  // open: gt, lt
  and and_18 (M2_SEL, M2_VO, comparator_6_eq);
  RS_FF rs_ff_4 (.S(or_7_out), .C(C), .R(M2_RS), .Q(M2_COM));  // open: nQ
  or or_7 (or_7_out, and_17_out, and_19_out);
  and and_19 (and_19_out, comparator_7_eq, M2_VO, com1);
  Comparator #(.Bits(4)) comparator_7 (.a(M2_inst), .b(com1_id), .eq(comparator_7_eq));  // open: gt, lt
  Comparator #(.Bits(4)) comparator_8 (.a(M2_inst), .b(com2_id), .eq(comparator_8_eq));  // open: gt, lt
  Register #(.Bits(4)) register_17 (.D(inst), .C(C), .en(M2_IE), .Q(M2_inst));
  Register register_18 (.D(epoch), .C(C), .en(M2_IE), .Q(M2_epoch));
  inst_comp inst_comp_3 (.A_id(ld_id), .A_ep(ld_ep), .B_id(M2_inst), .B_ep(M2_epoch), .A_old(inst_comp_3_a_old));
  inst_comp inst_comp_4 (.A_id(M2_inst), .A_ep(M2_epoch), .B_id(clr_id), .B_ep(clr_ep), .A_old(inst_comp_4_a_old));
  and and_20 (M2_CMP, M2_VO, comparator_5_eq, inst_comp_3_a_old, 1'b1);
  and and_21 (M2_CLR, inst_comp_4_a_old, clr);
  and and_22 (and_22_out, com2, M3_VO, comparator_12_eq);
  RS_FF rs_ff_5 (.S(M3_IE), .C(C), .R(M3_RS), .Q(M3_VO));  // open: nQ
  and and_23 (M3_CMP, M3_VO, comparator_9_eq, inst_comp_5_a_old, 1'b1);
  Comparator #(.Bits(32)) comparator_9 (.a(ld_addr), .b(M3_A), .eq(comparator_9_eq));  // open: gt, lt
  Register #(.Bits(32)) register_19 (.D(A), .C(C), .en(M3_DE), .Q(M3_A));
  Register #(.Bits(32)) register_20 (.D(D), .C(C), .en(M3_DE), .Q(M3_D));
  Register #(.Bits(2)) register_21 (.D(MD), .C(C), .en(M3_DE), .Q(M3_MD));
  Comparator #(.Bits(4)) comparator_10 (.a(M3_inst), .b(inst_W), .eq(comparator_10_eq));  // open: gt, lt
  and and_24 (M3_SEL, M3_VO, comparator_10_eq);
  RS_FF rs_ff_6 (.S(or_8_out), .C(C), .R(M3_RS), .Q(M3_COM));  // open: nQ
  or or_8 (or_8_out, and_22_out, and_25_out);
  and and_25 (and_25_out, comparator_11_eq, M3_VO, com1);
  Comparator #(.Bits(4)) comparator_11 (.a(M3_inst), .b(com1_id), .eq(comparator_11_eq));  // open: gt, lt
  Comparator #(.Bits(4)) comparator_12 (.a(M3_inst), .b(com2_id), .eq(comparator_12_eq));  // open: gt, lt
  Register #(.Bits(4)) register_22 (.D(inst), .C(C), .en(M3_IE), .Q(M3_inst));
  Register register_23 (.D(epoch), .C(C), .en(M3_IE), .Q(M3_epoch));
  inst_comp inst_comp_5 (.A_id(ld_id), .A_ep(ld_ep), .B_id(M3_inst), .B_ep(M3_epoch), .A_old(inst_comp_5_a_old));
  inst_comp inst_comp_6 (.A_id(M3_inst), .A_ep(M3_epoch), .B_id(clr_id), .B_ep(clr_ep), .A_old(inst_comp_6_a_old));
  and and_26 (M3_CLR, inst_comp_6_a_old, clr);
  RS_FF rs_ff_7 (.S(M4_IE), .C(C), .R(M4_RS), .Q(M4_VO));  // open: nQ
  Comparator #(.Bits(32)) comparator_13 (.a(ld_addr), .b(M4_A), .eq(comparator_13_eq));  // open: gt, lt
  Register #(.Bits(32)) register_24 (.D(A), .C(C), .en(M4_DE), .Q(M4_A));
  Register #(.Bits(32)) register_25 (.D(D), .C(C), .en(M4_DE), .Q(M4_D));
  Register #(.Bits(2)) register_26 (.D(MD), .C(C), .en(M4_DE), .Q(M4_MD));
  Comparator #(.Bits(4)) comparator_14 (.a(M4_inst), .b(inst_W), .eq(comparator_14_eq));  // open: gt, lt
  RS_FF rs_ff_8 (.S(or_9_out), .C(C), .R(M4_RS), .Q(M4_COM));  // open: nQ
  and and_27 (and_27_out, com2, M4_VO, comparator_16_eq);
  Comparator #(.Bits(4)) comparator_15 (.a(M4_inst), .b(com1_id), .eq(comparator_15_eq));  // open: gt, lt
  Comparator #(.Bits(4)) comparator_16 (.a(M4_inst), .b(com2_id), .eq(comparator_16_eq));  // open: gt, lt
  Register #(.Bits(4)) register_27 (.D(inst), .C(C), .en(M4_IE), .Q(M4_inst));
  Register register_28 (.D(epoch), .C(C), .en(M4_IE), .Q(M4_epoch));
  inst_comp inst_comp_7 (.A_id(ld_id), .A_ep(ld_ep), .B_id(M4_inst), .B_ep(M4_epoch), .A_old(inst_comp_7_a_old));
  inst_comp inst_comp_8 (.A_id(M4_inst), .A_ep(M4_epoch), .B_id(clr_id), .B_ep(clr_ep), .A_old(inst_comp_8_a_old));
  and and_28 (M4_CMP, M4_VO, comparator_13_eq, inst_comp_7_a_old, 1'b1);
  and and_29 (M4_SEL, M4_VO, comparator_14_eq);
  or or_9 (or_9_out, and_27_out, and_30_out);
  and and_30 (and_30_out, comparator_15_eq, M4_VO, com1);
  and and_31 (M4_CLR, inst_comp_8_a_old, clr);

  // Other names for the same wires on the sheet: clear = clr; comp_addr[31:0] = ld_addr; comp_ep = ld_ep;
  //   comp_id[3:0] = ld_id; ld_O[31:0] = ld_D; V_out = V
endmodule
